# Fritzing sketch Untitled Sketch1 (saved by Fritzing 0.9.3b)
breadboards: 1

parts:
  R1 = Basic Flex Resistor  # not connected
  R2 = Basic Flex Resistor  # not connected
  R3 = Basic Flex Resistor  # not connected
  R4 = Basic Flex Resistor  # not connected
  R5 = Basic Flex Resistor  # not connected
  J1 = Basic Force Sensing Resistor (FSR) [package=THT]  # not connected
  J2 = Basic Force Sensing Resistor (FSR) [package=THT]  # not connected
  J3 = Basic Force Sensing Resistor (FSR) [package=THT]  # not connected
  R6 = Resistor [tolerance=±5% resistance=220 package=THT]  # not connected
  R7 = Resistor [tolerance=±5% resistance=220 package=THT]  # not connected
  R8 = Resistor [tolerance=±5% resistance=220 package=THT]  # not connected
  R9 = Resistor [tolerance=±5% resistance=220 package=THT]  # not connected
  R10 = Resistor [tolerance=±5% resistance=220 package=THT]  # not connected
  ADC1 = MCP3008 [package=dil16]
  MCU1 = Raspberry Pi Zero
  부품2 = InvenSense MPU6050

nets:
  N1: ADC1.DGND, ADC1.VREF, ADC1.VDD, MCU1.pin_1
  N2: ADC1.CS/SHDN, MCU1.pin_24
  N3: ADC1.Dout, MCU1.pin_21
  N4: ADC1.CLK, MCU1.pin_19
  N5: ADC1.AGND, MCU1.pin_6, MCU1.pin_9, 부품2.GND
  N6: MCU1.pin_2, MCU1.pin_4, 부품2.VCC
  N7: MCU1.pin_3, 부품2.SDA
  N8: MCU1.pin_5, 부품2.SCL
